// Digital circuit 403102322_CPU.dig as structural Verilog
module _403102322_CPU (
  input  [15:0] DBG_MADDR,
  input  DBG_EN,
  input  [2:0] DBG_RSEL,
  input  RESET,
  input  CLK,
  output [7:0] PC_OUT,
  output [15:0] IR_OUT,
  output [3:0] FLAGS_OUT,
  output [15:0] DBG_MOUT,
  output [15:0] DBG_ROUT
);

  wire ALUSrcA, ALUSrcB, C, comparator_1_eq, Cond, en_Reg4flags, final_MemWr, FlagCapable, MemWr, N, RegDst,
       RegW, V, we_RF, Z;
  wire [1:0] final_PCSrc, PCSrc, WBSel;
  wire [2:0] ALUFunc, Rd_addr, Rs1_addr, Rs2_addr;
  wire [3:0] multiplexer_7_out;
  wire [7:0] add_1_s, multiplexer_2_out, multiplexer_3_out, PC_plus_1_se;
  wire [15:0] ALU_Reasult, imm4, imm7, multiplexer_4_out, multiplexer_5_out, multiplexer_6_out,
       multiplexer_11_out, ofset10, Rs1_data, Rs2_data, WBSel_MUX;

  Add #(.Bits(8)) add_1 (.a(PC_plus_1_se), .b(ofset10[7:0]), .c_i(1'b0), .s(add_1_s));  // open: c_o
  Multiplexer #(.Bits(2)) multiplexer_1 (.sel(Cond), .in_0(2'b00), .in_1(PCSrc), .out(final_PCSrc));
  ControlUnit controlunit_1 (
    .Opcode(IR_OUT[13:10]), .FlagCapable(FlagCapable), .PCSrc(PCSrc), .WBSel(WBSel), .MemWr(MemWr),
    .ALUFunc(ALUFunc), .ALUSrcB(ALUSrcB), .ALUSrcA(ALUSrcA), .RegDst(RegDst), .RegW(RegW));  // open: MemRd
  Multiplexer #(.Selector_Bits(2), .Bits(8)) multiplexer_2 (
    .sel(final_PCSrc), .in_0(PC_plus_1_se), .in_1(add_1_s), .in_2(Rs1_data[7:0]), .in_3({8{1'b0}}),
    .out(multiplexer_2_out));
  Multiplexer #(.Bits(8)) multiplexer_3 (
    .sel(RESET), .in_0(multiplexer_2_out), .in_1({8{1'b0}}), .out(multiplexer_3_out));
  Register #(.Bits(8)) PC (.D(multiplexer_3_out), .C(CLK), .en(1'b1), .Q(PC_OUT));
  Add #(.Bits(8)) add_2 (.a(8'h1), .b(PC_OUT), .c_i(1'b0), .s(PC_plus_1_se));  // open: c_o
  Multiplexer #(.Bits(16)) multiplexer_4 (.sel(comparator_1_eq), .in_0(imm4), .in_1(imm7), .out(multiplexer_4_out));
  Comparator #(.Bits(4)) comparator_1 (.a(4'b1010), .b(IR_OUT[13:10]), .eq(comparator_1_eq));  // open: gt, lt
  ROM #(.AddrBits(8), .isProgramMemory("true"), .Bits(16)) rom_1 (.A(PC_OUT), .sel(1'b1), .D(IR_OUT));
  Multiplexer #(.Bits(16)) multiplexer_5 (.sel(ALUSrcA), .in_0(Rs1_data), .in_1({16{1'b0}}), .out(multiplexer_5_out));
  Multiplexer #(.Bits(16)) multiplexer_6 (
    .sel(ALUSrcB), .in_0(Rs2_data), .in_1(multiplexer_4_out), .out(multiplexer_6_out));
  BitExtender #(.inputBits(4)) bitextender_1 (.in(IR_OUT[3:0]), .out(imm4));
  BitExtender #(.inputBits(7)) bitextender_2 (.in(IR_OUT[6:0]), .out(imm7));
  BitExtender #(.inputBits(10)) bitextender_3 (.in(IR_OUT[9:0]), .out(ofset10));
  // ALU_CPU alu_cpu_1: pin names not known; wires that end beside it: multiplexer_5_out, multiplexer_6_out, ALUFunc, ALU_Reasult, C, Z, N, V
  Multiplexer #(.Bits(4)) multiplexer_7 (.sel(RESET), .in_0({V, C, N, Z}), .in_1(4'b0000), .out(multiplexer_7_out));
  and and_1 (en_Reg4flags, IR_OUT[0], FlagCapable, Cond);
  Multiplexer #(.Bits(3)) multiplexer_8 (.sel(MemWr), .in_0(IR_OUT[3:1]), .in_1(IR_OUT[9:7]), .out(Rs2_addr));
  Multiplexer #(.Bits(3)) multiplexer_9 (.sel(PCSrc[1]), .in_0(IR_OUT[6:4]), .in_1(IR_OUT[9:7]), .out(Rs1_addr));
  Multiplexer #(.Selector_Bits(2), .Bits(16)) multiplexer_10 (
    .sel(WBSel), .in_0(ALU_Reasult), .in_1(DBG_MOUT), .in_2({IR_OUT[6:0], {9{1'b0}}}),
    .in_3({{8{1'b0}}, PC_plus_1_se}), .out(WBSel_MUX));
  Register #(.Bits(4)) register_1 (.D(multiplexer_7_out), .C(CLK), .en(en_Reg4flags), .Q(FLAGS_OUT));
  and and_2 (final_MemWr, MemWr, Cond);
  Multiplexer #(.Bits(16)) multiplexer_11 (
    .sel(DBG_EN), .in_0(ALU_Reasult), .in_1(DBG_MADDR), .out(multiplexer_11_out));
  Multiplexer #(.Selector_Bits(2)) multiplexer_12 (
    .sel(IR_OUT[15:14]), .in_0(1'b1), .in_1(FLAGS_OUT[0]), .in_2(FLAGS_OUT[1]), .in_3(FLAGS_OUT[3]),
    .out(Cond));
  Multiplexer #(.Bits(3)) multiplexer_13 (.sel(RegDst), .in_0(IR_OUT[9:7]), .in_1(3'b111), .out(Rd_addr));
  and and_3 (we_RF, Cond, RegW);
  RAMDualPort #(.AddrBits(16), .Bits(16)) DMEM (
    .A(multiplexer_11_out), .Din(Rs2_data), .str(final_MemWr), .C(CLK), .ld(1'b1), .D(DBG_MOUT));
  // RegisterFile_CPU registerfile_cpu_1: pin names not known; wires that end beside it: WBSel_MUX, we_RF, Rd_addr, CLK, Rs1_addr, Rs2_addr, DBG_EN, DBG_RSEL, Rs1_data, DBG_ROUT, Rs2_data

  // Other names for the same wires on the sheet: Z_new = FLAGS_OUT[0]; N_new = FLAGS_OUT[1]; C_new = FLAGS_OUT[2];
  //   V_new = FLAGS_OUT[3]; Imm7_BSE[6:0] = IR_OUT[6:0]; LUI_Result[15:9] = IR_OUT[6:0]; S = IR_OUT[0];
  //   IR_3_1[2:0] = IR_OUT[3:1]; IR_6_4[2:0] = IR_OUT[6:4]; IR_7_9[2:0] = IR_OUT[9:7]; Opcode[3:0] = IR_OUT[13:10];
  //   CC[1:0] = IR_OUT[15:14]; PCSrc_1 = PCSrc[1]
endmodule

/* Test case MOVI positive:
CLK RESET DBG_EN DBG_RSEL DBG_MADDR PC_OUT IR_OUT FLAGS_OUT DBG_ROUT DBG_MOUT

program(0x28bf,0x33ff)

0 0x0001 0 0 0 X X X X X
C 0x0001 0 0 0 X X X X X
loop(i,1)
C 0 0 0x0001 0 X X X X X
end loop
0 0 0x0001 0x0001 0 X X X 0x003f X
*/

/* Test case SHL:
CLK RESET DBG_EN DBG_RSEL DBG_MADDR PC_OUT IR_OUT FLAGS_OUT DBG_ROUT DBG_MOUT

program(0x2881,0x290f,0x1594,0x33ff)

0 0x0001 0 0 0 X X X X X
C 0x0001 0 0 0 X X X X X
loop(i,3)
C 0 0 0x0003 0 X X X X X
end loop
0 0 0x0001 0x0003 0 X X X 0x8000 X
*/

/* Test case no .S means the flags never change:
CLK RESET DBG_EN DBG_RSEL DBG_MADDR PC_OUT IR_OUT FLAGS_OUT DBG_ROUT DBG_MOUT

program(0x2887,0x2907,0x0595,0x2a01,0x2a82,0x074a,0x33ff)

0 0x0001 0 0 0 X X X X X
C 0x0001 0 0 0 X X X X X
loop(i,6)
C 0 0 0x0006 0 X X X X X
end loop
0 0 0x0001 0x0006 0 X X 0x0001 0xffff X
*/

/* Test case sort: random:
CLK RESET DBG_EN DBG_RSEL DBG_MADDR PC_OUT IR_OUT FLAGS_OUT DBG_ROUT DBG_MOUT

program(0x2890,0x2908,0x1d2f,0x0421,0x700e,0x0190,0x0314,0x043d,0xb001,0x33f8,0x2230,0x22b1,0x0459,0xb001,0x3002,0x26b0,0x2631,0x1db1,0x33f4,0x33ff)
memory DMEM(16) = 0x002a;
memory DMEM(17) = 0xfff9;
memory DMEM(18) = 0x0000;
memory DMEM(19) = 0x0384;
memory DMEM(20) = 0x0005;
memory DMEM(21) = 0x0005;
memory DMEM(22) = 0xffff;
memory DMEM(23) = 0x0080;

0 0x0001 0 0 0 X X X X X
C 0x0001 0 0 0 X X X X X
0 0 0 0 0 0x0000 X X X X
loop(i,1200)
C 0 0 0 0 X X X X X
end loop
# the program must have reached its final self-loop by now ...
0 0 0 0 0 0x0013 X X X X
loop(i,5)
C 0 0 0 0 X X X X X
end loop
# ... and must stay there
0 0 0 0 0 0x0013 X X X X
0 0 0x0001 0 0x0010 X X X X 0xfff9
0 0 0x0001 0 0x0011 X X X X 0xffff
0 0 0x0001 0 0x0012 X X X X 0x0000
0 0 0x0001 0 0x0013 X X X X 0x0005
0 0 0x0001 0 0x0014 X X X X 0x0005
0 0 0x0001 0 0x0015 X X X X 0x002a
0 0 0x0001 0 0x0016 X X X X 0x0080
0 0 0x0001 0 0x0017 X X X X 0x0384
*/

/* Test case far branches, forward and backward:
CLK RESET DBG_EN DBG_RSEL DBG_MADDR PC_OUT IR_OUT FLAGS_OUT DBG_ROUT DBG_MOUT

program(0x30c7,0x2907,0x33ff,0x0000,0x0000,0x0000,0x0000,0x0000,0x0000,0x0000,0x0000,0x0000,0x0000,0x0000,0x0000,0x0000,0x0000,0x0000,0x0000,0x0000,0x0000,0x0000,0x0000,0x0000,0x0000,0x0000,0x0000,0x0000,0x0000,0x0000,0x0000,0x0000,0x0000,0x0000,0x0000,0x0000,0x0000,0x0000,0x0000,0x0000,0x0000,0x0000,0x0000,0x0000,0x0000,0x0000,0x0000,0x0000,0x0000,0x0000,0x0000,0x0000,0x0000,0x0000,0x0000,0x0000,0x0000,0x0000,0x0000,0x0000,0x0000,0x0000,0x0000,0x0000,0x0000,0x0000,0x0000,0x0000,0x0000,0x0000,0x0000,0x0000,0x0000,0x0000,0x0000,0x0000,0x0000,0x0000,0x0000,0x0000,0x0000,0x0000,0x0000,0x0000,0x0000,0x0000,0x0000,0x0000,0x0000,0x0000,0x0000,0x0000,0x0000,0x0000,0x0000,0x0000,0x0000,0x0000,0x0000,0x0000,0x0000,0x0000,0x0000,0x0000,0x0000,0x0000,0x0000,0x0000,0x0000,0x0000,0x0000,0x0000,0x0000,0x0000,0x0000,0x0000,0x0000,0x0000,0x0000,0x0000,0x0000,0x0000,0x0000,0x0000,0x0000,0x0000,0x0000,0x0000,0x0000,0x0000,0x0000,0x0000,0x0000,0x0000,0x0000,0x0000,0x0000,0x0000,0x0000,0x0000,0x0000,0x0000,0x0000,0x0000,0x0000,0x0000,0x0000,0x0000,0x0000,0x0000,0x0000,0x0000,0x0000,0x0000,0x0000,0x0000,0x0000,0x0000,0x0000,0x0000,0x0000,0x0000,0x0000,0x0000,0x0000,0x0000,0x0000,0x0000,0x0000,0x0000,0x0000,0x0000,0x0000,0x0000,0x0000,0x0000,0x0000,0x0000,0x0000,0x0000,0x0000,0x0000,0x0000,0x0000,0x0000,0x0000,0x0000,0x0000,0x0000,0x0000,0x0000,0x0000,0x0000,0x0000,0x0000,0x0000,0x0000,0x0000,0x0000,0x0000,0x2883,0x3337)

0 0x0001 0 0 0 X X X X X
C 0x0001 0 0 0 X X X X X
0 0 0 0 0 0x0000 X X X X
C 0 0 0 0 X X X X X
# forward branch of +199 landed
0 0 0 0 0 0x00c8 X X X X
C 0 0 0 0 X X X X X
C 0 0 0 0 X X X X X
# backward branch of -201 landed
0 0 0 0 0 0x0001 X X X X
C 0 0 0 0 X X X X X
0 0 0x0001 0x0002 0 X X X 0x0007 X
*/

/* Test case MOVI negative (sign extended):
CLK RESET DBG_EN DBG_RSEL DBG_MADDR PC_OUT IR_OUT FLAGS_OUT DBG_ROUT DBG_MOUT

program(0x28c0,0x33ff)

0 0x0001 0 0 0 X X X X X
C 0x0001 0 0 0 X X X X X
loop(i,1)
C 0 0 0x0001 0 X X X X X
end loop
0 0 0x0001 0x0001 0 X X X 0xffc0 X
*/

/* Test case SHR:
CLK RESET DBG_EN DBG_RSEL DBG_MADDR PC_OUT IR_OUT FLAGS_OUT DBG_ROUT DBG_MOUT

program(0x2881,0x290f,0x1494,0x290c,0x1994,0x33ff)

0 0x0001 0 0 0 X X X X X
C 0x0001 0 0 0 X X X X X
loop(i,5)
C 0 0 0x0003 0 X X X X X
end loop
0 0 0x0001 0x0003 0 X X X 0x0008 X
*/

/* Test case LW and SW:
CLK RESET DBG_EN DBG_RSEL DBG_MADDR PC_OUT IR_OUT FLAGS_OUT DBG_ROUT DBG_MOUT

program(0x2890,0x2110,0x1d23,0x2511,0x33ff)
memory DMEM(16) = 0x0061;

0 0x0001 0 0 0 X X X X X
C 0x0001 0 0 0 X X X X X
loop(i,4)
C 0 0 0 0 X X X X X
end loop
0 0 0x0001 0x0002 0x0011 X X X 0x0064 0x0064
*/

/* Test case sort: already sorted:
CLK RESET DBG_EN DBG_RSEL DBG_MADDR PC_OUT IR_OUT FLAGS_OUT DBG_ROUT DBG_MOUT

program(0x2890,0x2908,0x1d2f,0x0421,0x700e,0x0190,0x0314,0x043d,0xb001,0x33f8,0x2230,0x22b1,0x0459,0xb001,0x3002,0x26b0,0x2631,0x1db1,0x33f4,0x33ff)
memory DMEM(16) = 0x0001;
memory DMEM(17) = 0x0002;
memory DMEM(18) = 0x0003;
memory DMEM(19) = 0x0004;
memory DMEM(20) = 0x0005;
memory DMEM(21) = 0x0006;
memory DMEM(22) = 0x0007;
memory DMEM(23) = 0x0008;

0 0x0001 0 0 0 X X X X X
C 0x0001 0 0 0 X X X X X
0 0 0 0 0 0x0000 X X X X
loop(i,1200)
C 0 0 0 0 X X X X X
end loop
# the program must have reached its final self-loop by now ...
0 0 0 0 0 0x0013 X X X X
loop(i,5)
C 0 0 0 0 X X X X X
end loop
# ... and must stay there
0 0 0 0 0 0x0013 X X X X
0 0 0x0001 0 0x0010 X X X X 0x0001
0 0 0x0001 0 0x0011 X X X X 0x0002
0 0 0x0001 0 0x0012 X X X X 0x0003
0 0 0x0001 0 0x0013 X X X X 0x0004
0 0 0x0001 0 0x0014 X X X X 0x0005
0 0 0x0001 0 0x0015 X X X X 0x0006
0 0 0x0001 0 0x0016 X X X X 0x0007
0 0 0x0001 0 0x0017 X X X X 0x0008
*/

/* Test case sum: all positive:
CLK RESET DBG_EN DBG_RSEL DBG_MADDR PC_OUT IR_OUT FLAGS_OUT DBG_ROUT DBG_MOUT

program(0x2890,0x2908,0x2a00,0x0421,0x7005,0x2190,0x0246,0x1c91,0x1d2f,0x33f9,0x2600,0x33ff)
memory DMEM(16) = 0x0005;
memory DMEM(17) = 0x0003;
memory DMEM(18) = 0x000c;
memory DMEM(19) = 0x0001;
memory DMEM(20) = 0x0028;
memory DMEM(21) = 0x0007;
memory DMEM(22) = 0x0002;
memory DMEM(23) = 0x001e;

0 0x0001 0 0 0 X X X X X
C 0x0001 0 0 0 X X X X X
0 0 0 0 0 0x0000 X X X X
loop(i,200)
C 0 0 0 0 X X X X X
end loop
# the program must have reached its final self-loop by now ...
0 0 0 0 0 0x000b X X X X
loop(i,5)
C 0 0 0 0 X X X X X
end loop
# ... and must stay there
0 0 0 0 0 0x000b X X X X
0 0 0x0001 0 0x0000 X X X X 0x0064
*/

/* Test case LUI puts imm7 into bits 15..9:
CLK RESET DBG_EN DBG_RSEL DBG_MADDR PC_OUT IR_OUT FLAGS_OUT DBG_ROUT DBG_MOUT

program(0x2cc0,0x2d09,0x33ff)

0 0x0001 0 0 0 X X X X X
C 0x0001 0 0 0 X X X X X
loop(i,2)
C 0 0 0 0 X X X X X
end loop
0 0 0x0001 0x0001 0 X X X 0x8000 X
0 0 0x0001 0x0002 0 X X X 0x1200 X
*/

/* Test case R0 is hard wired to zero:
CLK RESET DBG_EN DBG_RSEL DBG_MADDR PC_OUT IR_OUT FLAGS_OUT DBG_ROUT DBG_MOUT

program(0x282a,0x33ff)

0 0x0001 0 0 0 X X X X X
C 0x0001 0 0 0 X X X X X
loop(i,1)
C 0 0 0x0000 0 X X X X X
end loop
0 0 0x0001 0x0000 0 X X X 0x0000 X
*/

/* Test case ADDI:
CLK RESET DBG_EN DBG_RSEL DBG_MADDR PC_OUT IR_OUT FLAGS_OUT DBG_ROUT DBG_MOUT

program(0x288a,0x1d18,0x33ff)

0 0x0001 0 0 0 X X X X X
C 0x0001 0 0 0 X X X X X
loop(i,2)
C 0 0 0x0002 0 X X X X X
end loop
0 0 0x0001 0x0002 0 X X X 0x0002 X
*/

/* Test case predicated execution (.EQ taken, .LT suppressed):
CLK RESET DBG_EN DBG_RSEL DBG_MADDR PC_OUT IR_OUT FLAGS_OUT DBG_ROUT DBG_MOUT

program(0x2887,0x2907,0x0415,0x2981,0x41b2,0x2a01,0x8242,0x33ff)

0 0x0001 0 0 0 X X X X X
C 0x0001 0 0 0 X X X X X
loop(i,7)
C 0 0 0 0 X X X X X
end loop
0 0 0x0001 0x0003 0 X X X 0x0008 X
0 0 0x0001 0x0004 0 X X X 0x0001 X
*/

/* Test case sort: reverse sorted:
CLK RESET DBG_EN DBG_RSEL DBG_MADDR PC_OUT IR_OUT FLAGS_OUT DBG_ROUT DBG_MOUT

program(0x2890,0x2908,0x1d2f,0x0421,0x700e,0x0190,0x0314,0x043d,0xb001,0x33f8,0x2230,0x22b1,0x0459,0xb001,0x3002,0x26b0,0x2631,0x1db1,0x33f4,0x33ff)
memory DMEM(16) = 0x0008;
memory DMEM(17) = 0x0007;
memory DMEM(18) = 0x0006;
memory DMEM(19) = 0x0005;
memory DMEM(20) = 0x0004;
memory DMEM(21) = 0x0003;
memory DMEM(22) = 0x0002;
memory DMEM(23) = 0x0001;

0 0x0001 0 0 0 X X X X X
C 0x0001 0 0 0 X X X X X
0 0 0 0 0 0x0000 X X X X
loop(i,1200)
C 0 0 0 0 X X X X X
end loop
# the program must have reached its final self-loop by now ...
0 0 0 0 0 0x0013 X X X X
loop(i,5)
C 0 0 0 0 X X X X X
end loop
# ... and must stay there
0 0 0 0 0 0x0013 X X X X
0 0 0x0001 0 0x0010 X X X X 0x0001
0 0 0x0001 0 0x0011 X X X X 0x0002
0 0 0x0001 0 0x0012 X X X X 0x0003
0 0 0x0001 0 0x0013 X X X X 0x0004
0 0 0x0001 0 0x0014 X X X X 0x0005
0 0 0x0001 0 0x0015 X X X X 0x0006
0 0 0x0001 0 0x0016 X X X X 0x0007
0 0 0x0001 0 0x0017 X X X X 0x0008
*/

/* Test case sum: mixed signs:
CLK RESET DBG_EN DBG_RSEL DBG_MADDR PC_OUT IR_OUT FLAGS_OUT DBG_ROUT DBG_MOUT

program(0x2890,0x2908,0x2a00,0x0421,0x7005,0x2190,0x0246,0x1c91,0x1d2f,0x33f9,0x2600,0x33ff)
memory DMEM(16) = 0xfffb;
memory DMEM(17) = 0x0003;
memory DMEM(18) = 0xfff4;
memory DMEM(19) = 0x0001;
memory DMEM(20) = 0xffd8;
memory DMEM(21) = 0x0007;
memory DMEM(22) = 0xfffe;
memory DMEM(23) = 0x001e;

0 0x0001 0 0 0 X X X X X
C 0x0001 0 0 0 X X X X X
0 0 0 0 0 0x0000 X X X X
loop(i,200)
C 0 0 0 0 X X X X X
end loop
# the program must have reached its final self-loop by now ...
0 0 0 0 0 0x000b X X X X
loop(i,5)
C 0 0 0 0 X X X X X
end loop
# ... and must stay there
0 0 0 0 0 0x000b X X X X
0 0 0x0001 0 0x0000 X X X X 0xffee
*/

/* Test case JR uses only the low 8 bits of Rs1:
CLK RESET DBG_EN DBG_RSEL DBG_MADDR PC_OUT IR_OUT FLAGS_OUT DBG_ROUT DBG_MOUT

program(0x2c89,0x1c97,0x3880,0x2981,0x2982,0x2983,0x2984,0x2989,0x33ff)

0 0x0001 0 0 0 X X X X X
C 0x0001 0 0 0 X X X X X
loop(i,3)
C 0 0 0 0 X X X X X
end loop
# only the low 8 bits of R1 reach the PC
0 0 0 0 0 0x0007 X X X X
C 0 0 0 0 X X X X X
0 0 0x0001 0x0003 0 X X X 0x0009 X
*/

/* Test case reset and fetch protocol:
CLK RESET DBG_EN DBG_RSEL DBG_MADDR PC_OUT IR_OUT FLAGS_OUT DBG_ROUT DBG_MOUT

program(0x2885,0x2909,0x0194,0x33ff)

0 0x0001 0 0 0 X X X X X
C 0x0001 0 0 0 X X X X X
# after reset the PC is 0 and the first instruction is visible
0 0 0 0 0 0x0000 0x2885 0x0000 X X
# one clock pulse == exactly one instruction
C 0 0 0 0 X X X X X
0 0 0 0 0 0x0001 0x2909 X X X
C 0 0 0 0 X X X X X
0 0 0 0 0 0x0002 0x0194 X X X
C 0 0 0 0 X X X X X
0 0 0 0 0 0x0003 0x33ff X X X
# HALT is a branch to itself, so the PC stays on it for ever
loop(i,20)
C 0 0 0 0 X X X X X
end loop
0 0 0 0 0 0x0003 0x33ff X X X
*/

/* Test case ADD:
CLK RESET DBG_EN DBG_RSEL DBG_MADDR PC_OUT IR_OUT FLAGS_OUT DBG_ROUT DBG_MOUT

program(0x2894,0x297b,0x0194,0x33ff)

0 0x0001 0 0 0 X X X X X
C 0x0001 0 0 0 X X X X X
loop(i,3)
C 0 0 0x0003 0 X X X X X
end loop
0 0 0x0001 0x0003 0 X X X 0x000f X
*/

/* Test case flags: zero:
CLK RESET DBG_EN DBG_RSEL DBG_MADDR PC_OUT IR_OUT FLAGS_OUT DBG_ROUT DBG_MOUT

program(0x2887,0x2907,0x0595,0x33ff)

0 0x0001 0 0 0 X X X X X
C 0x0001 0 0 0 X X X X X
loop(i,3)
C 0 0 0x0003 0 X X X X X
end loop
0 0 0x0001 0x0003 0 X X 0x0001 0x0000 X
*/

/* Test case conditional branch taken and not taken:
CLK RESET DBG_EN DBG_RSEL DBG_MADDR PC_OUT IR_OUT FLAGS_OUT DBG_ROUT DBG_MOUT

program(0x2887,0x2907,0x0415,0x2980,0x7001,0x29bc,0x2a05,0xb001,0x2a81,0x33ff)

0 0x0001 0 0 0 X X X X X
C 0x0001 0 0 0 X X X X X
loop(i,10)
C 0 0 0 0 X X X X X
end loop
0 0 0x0001 0x0003 0 X X X 0x0000 X
0 0 0x0001 0x0005 0 X X X 0x0001 X
*/

/* Test case sort: all equal:
CLK RESET DBG_EN DBG_RSEL DBG_MADDR PC_OUT IR_OUT FLAGS_OUT DBG_ROUT DBG_MOUT

program(0x2890,0x2908,0x1d2f,0x0421,0x700e,0x0190,0x0314,0x043d,0xb001,0x33f8,0x2230,0x22b1,0x0459,0xb001,0x3002,0x26b0,0x2631,0x1db1,0x33f4,0x33ff)
memory DMEM(16) = 0x0004;
memory DMEM(17) = 0x0004;
memory DMEM(18) = 0x0004;
memory DMEM(19) = 0x0004;
memory DMEM(20) = 0x0004;
memory DMEM(21) = 0x0004;
memory DMEM(22) = 0x0004;
memory DMEM(23) = 0x0004;

0 0x0001 0 0 0 X X X X X
C 0x0001 0 0 0 X X X X X
0 0 0 0 0 0x0000 X X X X
loop(i,1200)
C 0 0 0 0 X X X X X
end loop
# the program must have reached its final self-loop by now ...
0 0 0 0 0 0x0013 X X X X
loop(i,5)
C 0 0 0 0 X X X X X
end loop
# ... and must stay there
0 0 0 0 0 0x0013 X X X X
0 0 0x0001 0 0x0010 X X X X 0x0004
0 0 0x0001 0 0x0011 X X X X 0x0004
0 0 0x0001 0 0x0012 X X X X 0x0004
0 0 0x0001 0 0x0013 X X X X 0x0004
0 0 0x0001 0 0x0014 X X X X 0x0004
0 0 0x0001 0 0x0015 X X X X 0x0004
0 0 0x0001 0 0x0016 X X X X 0x0004
0 0 0x0001 0 0x0017 X X X X 0x0004
*/

/* Test case sum: all zero:
CLK RESET DBG_EN DBG_RSEL DBG_MADDR PC_OUT IR_OUT FLAGS_OUT DBG_ROUT DBG_MOUT

program(0x2890,0x2908,0x2a00,0x0421,0x7005,0x2190,0x0246,0x1c91,0x1d2f,0x33f9,0x2600,0x33ff)
memory DMEM(16) = 0x0000;
memory DMEM(17) = 0x0000;
memory DMEM(18) = 0x0000;
memory DMEM(19) = 0x0000;
memory DMEM(20) = 0x0000;
memory DMEM(21) = 0x0000;
memory DMEM(22) = 0x0000;
memory DMEM(23) = 0x0000;

0 0x0001 0 0 0 X X X X X
C 0x0001 0 0 0 X X X X X
0 0 0 0 0 0x0000 X X X X
loop(i,200)
C 0 0 0 0 X X X X X
end loop
# the program must have reached its final self-loop by now ...
0 0 0 0 0 0x000b X X X X
loop(i,5)
C 0 0 0 0 X X X X X
end loop
# ... and must stay there
0 0 0 0 0 0x000b X X X X
0 0 0x0001 0 0x0000 X X X X 0x0000
*/

/* Test case JAL saves the return address in R7:
CLK RESET DBG_EN DBG_RSEL DBG_MADDR PC_OUT IR_OUT FLAGS_OUT DBG_ROUT DBG_MOUT

program(0x3402,0x2905,0x33ff,0x2a08,0x3b80)

0 0x0001 0 0 0 X X X X X
C 0x0001 0 0 0 X X X X X
0 0 0 0 0 0x0000 X X X X
C 0 0 0 0 X X X X X
# jumped into the subroutine
0 0 0 0 0 0x0003 X X X X
C 0 0 0 0 X X X X X
C 0 0 0 0 X X X X X
# and came back to the instruction after JAL
0 0 0 0 0 0x0001 X X X X
C 0 0 0 0 X X X X X
# R7 holds PC+1 of the JAL, zero extended into 16 bits
0 0 0x0001 0x0007 0 X X X 0x0001 X
0 0 0x0001 0x0004 0 X X X 0x0008 X
0 0 0x0001 0x0002 0 X X X 0x0005 X
*/

/* Test case SUB:
CLK RESET DBG_EN DBG_RSEL DBG_MADDR PC_OUT IR_OUT FLAGS_OUT DBG_ROUT DBG_MOUT

program(0x2894,0x297b,0x0594,0x33ff)

0 0x0001 0 0 0 X X X X X
C 0x0001 0 0 0 X X X X X
loop(i,3)
C 0 0 0x0003 0 X X X X X
end loop
0 0 0x0001 0x0003 0 X X X 0x0019 X
*/

/* Test case flags: negative and borrow:
CLK RESET DBG_EN DBG_RSEL DBG_MADDR PC_OUT IR_OUT FLAGS_OUT DBG_ROUT DBG_MOUT

program(0x2883,0x2905,0x0595,0x33ff)

0 0x0001 0 0 0 X X X X X
C 0x0001 0 0 0 X X X X X
loop(i,3)
C 0 0 0x0003 0 X X X X X
end loop
0 0 0x0001 0x0003 0 X X 0x0006 0xfffe X
*/

/* Test case reset from the middle of a program:
CLK RESET DBG_EN DBG_RSEL DBG_MADDR PC_OUT IR_OUT FLAGS_OUT DBG_ROUT DBG_MOUT

program(0x2885,0x2909,0x0194,0x33ff)

0 0x0001 0 0 0 X X X X X
C 0x0001 0 0 0 X X X X X
loop(i,3)
C 0 0 0 0 X X X X X
end loop
0 0 0 0 0 0x0003 X X X X
0 0x0001 0 0 0 X X X X X
C 0x0001 0 0 0 X X X X X
0 0 0 0 0 0x0000 0x2885 0x0000 X X
*/

/* Test case sort: extremes:
CLK RESET DBG_EN DBG_RSEL DBG_MADDR PC_OUT IR_OUT FLAGS_OUT DBG_ROUT DBG_MOUT

program(0x2890,0x2908,0x1d2f,0x0421,0x700e,0x0190,0x0314,0x043d,0xb001,0x33f8,0x2230,0x22b1,0x0459,0xb001,0x3002,0x26b0,0x2631,0x1db1,0x33f4,0x33ff)
memory DMEM(16) = 0x03e8;
memory DMEM(17) = 0xfc18;
memory DMEM(18) = 0x03e7;
memory DMEM(19) = 0xfc19;
memory DMEM(20) = 0x0000;
memory DMEM(21) = 0x0001;
memory DMEM(22) = 0xffff;
memory DMEM(23) = 0x01f4;

0 0x0001 0 0 0 X X X X X
C 0x0001 0 0 0 X X X X X
0 0 0 0 0 0x0000 X X X X
loop(i,1200)
C 0 0 0 0 X X X X X
end loop
# the program must have reached its final self-loop by now ...
0 0 0 0 0 0x0013 X X X X
loop(i,5)
C 0 0 0 0 X X X X X
end loop
# ... and must stay there
0 0 0 0 0 0x0013 X X X X
0 0 0x0001 0 0x0010 X X X X 0xfc18
0 0 0x0001 0 0x0011 X X X X 0xfc19
0 0 0x0001 0 0x0012 X X X X 0xffff
0 0 0x0001 0 0x0013 X X X X 0x0000
0 0 0x0001 0 0x0014 X X X X 0x0001
0 0 0x0001 0 0x0015 X X X X 0x01f4
0 0 0x0001 0 0x0016 X X X X 0x03e7
0 0 0x0001 0 0x0017 X X X X 0x03e8
*/

/* Test case a predicated JAL that is not taken writes nothing:
CLK RESET DBG_EN DBG_RSEL DBG_MADDR PC_OUT IR_OUT FLAGS_OUT DBG_ROUT DBG_MOUT

program(0x2b95,0x2883,0x2904,0x0415,0x7401,0x2a86,0x33ff)

0 0x0001 0 0 0 X X X X X
C 0x0001 0 0 0 X X X X X
loop(i,5)
C 0 0 0 0 X X X X X
end loop
# the conditional JAL was skipped, so R7 still holds the sentinel
0 0 0x0001 0x0007 0 X X X 0x0015 X
C 0 0 0 0 X X X X X
0 0 0x0001 0x0005 0 X X X 0x0006 X
*/

/* Test case AND / OR / XOR:
CLK RESET DBG_EN DBG_RSEL DBG_MADDR PC_OUT IR_OUT FLAGS_OUT DBG_ROUT DBG_MOUT

program(0x288c,0x290a,0x0994,0x0e14,0x1294,0x33ff)

0 0x0001 0 0 0 X X X X X
C 0x0001 0 0 0 X X X X X
loop(i,5)
C 0 0 0x0005 0 X X X X X
end loop
0 0 0x0001 0x0005 0 X X X 0x0006 X
*/

/* Test case flags: signed overflow:
CLK RESET DBG_EN DBG_RSEL DBG_MADDR PC_OUT IR_OUT FLAGS_OUT DBG_ROUT DBG_MOUT

program(0x2881,0x290f,0x1494,0x0193,0x33ff)

0 0x0001 0 0 0 X X X X X
C 0x0001 0 0 0 X X X X X
loop(i,4)
C 0 0 0x0003 0 X X X X X
end loop
0 0 0x0001 0x0003 0 X X 0x000d 0x0000 X
*/

/* Test case NOP changes nothing:
CLK RESET DBG_EN DBG_RSEL DBG_MADDR PC_OUT IR_OUT FLAGS_OUT DBG_ROUT DBG_MOUT

program(0x2895,0x3c00,0x3c00,0x33ff)

0 0x0001 0 0 0 X X X X X
C 0x0001 0 0 0 X X X X X
loop(i,1)
C 0 0 0 0 X X X X X
end loop
0 0 0 0 0 0x0001 0x3c00 X X X
loop(i,2)
C 0 0 0 0 X X X X X
end loop
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*/
