// Digital circuit ALU.dig as structural Verilog
module ALU (
  input  [15:0] A,
  input  [15:0] B,
  input  [2:0] ALUFunc,
  output [15:0] Result,
  output C,
  output Z,
  output N,
  output V
);

  wire add_2_c_o, and_2_out, and_3_out, sub_2_c_o, xnor_1_out, xor_2_out, xor_3_out, xor_4_out;
  wire [15:0] add_1_s, add_3_s, and_1_out, barrelshifter_1_out, barrelshifter_2_out, or_1_out, sub_1_s,
       sub_3_s, xor_1_out;

  assign and_1_out = A & B;  // And and_1, 16 bits wide
  assign or_1_out = A | B;  // Or or_1, 16 bits wide
  assign xor_1_out = A ^ B;  // XOr xor_1, 16 bits wide
  Add #(.Bits(16)) add_1 (.a(A), .b(B), .c_i(1'b0), .s(add_1_s));  // open: c_o
  Sub #(.Bits(16)) sub_1 (.a(A), .b(B), .c_i(1'b0), .s(sub_1_s));  // open: c_o
  BarrelShifter #(.Bits(16)) barrelshifter_1 (.in(A), .shift({1'b0, B[3:0]}), .out(barrelshifter_1_out));
  BarrelShifter #(.Bits(16), .direction("right")) barrelshifter_2 (
    .in(A), .shift({1'b0, B[3:0]}), .out(barrelshifter_2_out));
  Multiplexer #(.Selector_Bits(3), .Bits(16)) multiplexer_1 (
    .sel(ALUFunc), .in_0(add_1_s), .in_1(sub_1_s), .in_2(and_1_out), .in_3(or_1_out), .in_4(xor_1_out),
    .in_5(barrelshifter_1_out), .in_6(barrelshifter_2_out), .in_7({16{1'b0}}), .out({N, Result[14:0]}));
  Add #(.Bits(16)) add_2 (.a(A), .b(B), .c_i(1'b0), .c_o(add_2_c_o));  // open: s
  Sub #(.Bits(16)) sub_2 (.a(A), .b(B), .c_i(1'b0), .c_o(sub_2_c_o));  // open: s
  Comparator #(.Bits(16)) comparator_1 (.a({N, Result[14:0]}), .b({16{1'b0}}), .eq(Z));  // open: gt, lt
  Multiplexer #(.Selector_Bits(3)) multiplexer_2 (
    .sel(ALUFunc), .in_0(add_2_c_o), .in_1(sub_2_c_o), .in_2(1'b0), .in_3(1'b0), .in_4(1'b0), .in_5(1'b0),
    .in_6(1'b0), .in_7(1'b0), .out(C));
  Add #(.Bits(16)) add_3 (.a(A), .b(B), .c_i(1'b0), .s(add_3_s));  // open: c_o
  Sub #(.Bits(16)) sub_3 (.a(A), .b(B), .c_i(1'b0), .s(sub_3_s));  // open: c_o
  xor xor_2 (xor_2_out, A[15], B[15]);
  xnor xnor_1 (xnor_1_out, A[15], B[15]);
  xor xor_3 (xor_3_out, A[15], add_3_s[15]);
  xor xor_4 (xor_4_out, A[15], sub_3_s[15]);
  and and_2 (and_2_out, xnor_1_out, xor_3_out);
  and and_3 (and_3_out, xor_2_out, xor_4_out);
  Multiplexer #(.Selector_Bits(3)) multiplexer_3 (
    .sel(ALUFunc), .in_0(and_2_out), .in_1(and_3_out), .in_2(1'b0), .in_3(1'b0), .in_4(1'b0), .in_5(1'b0),
    .in_6(1'b0), .in_7(1'b0), .out(V));

  assign Result[15] = N;
endmodule
