// Digital circuit ControlUnit.dig as structural Verilog
module ControlUnit (
  input  [3:0] Opcode,
  output FlagCapable,
  output [1:0] PCSrc,
  output [1:0] WBSel,
  output MemRd,
  output MemWr,
  output [2:0] ALUFunc,
  output ALUSrcB,
  output ALUSrcA,
  output RegDst,
  output RegW
);

  ROM #(.AddrBits(4), .Bits(14)) rom_1 (
    .A(Opcode), .sel(1'b1),
    .D({RegW, RegDst, ALUSrcA, ALUSrcB, ALUFunc, MemWr, MemRd, WBSel, PCSrc, FlagCapable}));

  // Notes on the sheet:
  //   contents of rom_1 (hex, n*v repeats v):
  //   2001,2081,2101,2181,2201,2281,2301,2400,2428,440,2c00,2010,2,301a,4
endmodule
