// Digital circuit RegisterFile.dig as structural Verilog
module RegisterFile (
  input  [15:0] Write_Data,
  input  RegW,
  input  [2:0] Rd_addr,
  input  CLK,
  input  [2:0] Rs1_addr,
  input  [2:0] Rs2_addr,
  input  DBG_EN,
  input  [2:0] DBG_RSEL,
  output [15:0] Rs1_data,
  output [15:0] DBG_ROUT,
  output [15:0] Rs2_data
);

  wire comparator_1_eq, comparator_2_eq, comparator_3_eq, we;
  wire [2:0] multiplexer_2_out;
  wire [15:0] Da, Db;

  Comparator #(.Bits(3)) comparator_1 (.a(Rd_addr), .b(3'b000), .eq(comparator_1_eq));  // open: gt, lt
  Multiplexer multiplexer_1 (.sel(comparator_1_eq), .in_0(RegW), .in_1(1'b0), .out(we));
  Multiplexer #(.Bits(3)) multiplexer_2 (.sel(DBG_EN), .in_0(Rs2_addr), .in_1(DBG_RSEL), .out(multiplexer_2_out));
  RegisterFile #(.AddrBits(3), .Bits(16)) registerfile_1 (
    .Din(Write_Data), .we(we), .Rw(Rd_addr), .C(CLK), .Ra(Rs1_addr), .Rb(multiplexer_2_out), .Da(Da), .Db(Db));
  Comparator #(.Bits(3)) comparator_2 (.a(Rs1_addr), .b(3'b000), .eq(comparator_2_eq));  // open: gt, lt
  Comparator #(.Bits(3)) comparator_3 (.a(multiplexer_2_out), .b(3'b000), .eq(comparator_3_eq));  // open: gt, lt
  Multiplexer #(.Bits(16)) multiplexer_3 (.sel(comparator_2_eq), .in_0(Da), .in_1({16{1'b0}}), .out(Rs1_data));
  Multiplexer #(.Bits(16)) multiplexer_4 (.sel(comparator_3_eq), .in_0(Db), .in_1({16{1'b0}}), .out(DBG_ROUT));

  assign Rs2_data = DBG_ROUT;
endmodule
